# Fritzing sketch lerSensor_01 (saved by Fritzing 0.9.3b)
breadboards: 1

parts:
  Part1 = Arduino Nano (Rev3.0) (ICSP)
  U1 = POT [package=pot_alpha_rv16af-20]

nets:
  N1: Part1.GND, U1.E
  N2: Part1.5V, U1.A
  N3: Part1.A0, U1.S
