# Fritzing sketch piezo_led (saved by Fritzing 0.9.3b)
breadboards: 1

parts:
  Part1 = Arduino Nano (Rev3.0) (ICSP)
  J1 = Piezo Speaker
  R1 = Resistor [tolerance=±5% resistance=220 package="0603 [SMD]"]
  LED1 = LED - 5mm [color="Red (633nm)" package="5 mm [THT]"]

nets:
  N1: Part1.GND, J1.pin1, R1.Pin_1, LED1.cathode
  N2: Part1.D2, LED1.anode
  N3: Part1.A0, J1.pin2, R1.Pin_0
